// Logisim project shootThatShipDemo.circ as structural Verilog: 14 circuits, main circuit main
module main (
  input  in_1,
  input  in_2,
  input  in_3,
  input  in_4,
  input  in_5,
  output [3:0] out_6,
  output [15:0] \output ,
  output [2:0] out_8,
  output [1:0] out_9,
  output [2:0] out_10,
  output [15:0] out_11,
  output [15:0] output_2
);

  wire adder_1_output, and_1_out, and_2_out, autoload_2_output_1, autoload_2_output_2, autoload_2_output_3,
       autoload_2_output_4, boom, button_5_out, clear, clock, clock_1_out, clock_2_out, \cross , d_ff_1_q,
       d_ff_2_q, d_ff_2_qn, d_ff_3_q, holdtobutton_1_output, HoldToNextLocation, Load, LoadAlldata, LoadPic,
       LoadTemp, miss, not_1_out, not_2_out, resetGame, save, unknown, updatePlayer, UpdateTemp0,
       UpdateTemp1, UpdateTemp2, UpdateTemp3, UpdateTemp4, UpdateTemp5, UpdateTemp6, UpdateTemp7,
       UpdateTemp8, UpdateTemp9, UpdateTemp10, UpdateTemp11, UpdateTemp12, UpdateTemp13, UpdateTemp14,
       UpdateTemp15, WinTheGame;
  wire [2:0] demultiplexer_2_out0, demultiplexer_2_out1, demultiplexer_2_out2, demultiplexer_2_out3,
       demultiplexer_2_out4, demultiplexer_2_out5, demultiplexer_2_out6, demultiplexer_2_out7,
       demultiplexer_2_out8, demultiplexer_2_out9, demultiplexer_2_out10, demultiplexer_2_out11,
       demultiplexer_2_out12, demultiplexer_2_out13, demultiplexer_2_out14, demultiplexer_2_out15, p1, p2,
       p3, p4, p5, p6, p7, p8, p9, p10, p11, p12, p13, p14, p15, picselector_1_output;
  wire [3:0] bit_extender_1_out, register_1_q;
  wire [7:0] display_1_out_2, display_1_out_3, display_1_out_4, display_1_out_5, display_1_out_6,
       display_1_out_7, display_1_out_8, display_1_out_9, display_2_out_2, display_2_out_3, display_2_out_4,
       display_2_out_5, display_2_out_6, display_2_out_7, display_2_out_8, display_2_out_9, display_3_out_2,
       display_3_out_3, display_3_out_4, display_3_out_5, display_3_out_6, display_3_out_7, display_3_out_8,
       display_3_out_9, display_4_out_2, display_4_out_3, display_4_out_4, display_4_out_5, display_4_out_6,
       display_4_out_7, display_4_out_8, display_4_out_9, display_5_out_2, display_5_out_3, display_5_out_4,
       display_5_out_5, display_5_out_6, display_5_out_7, display_5_out_8, display_5_out_9, display_6_out_2,
       display_6_out_3, display_6_out_4, display_6_out_5, display_6_out_6, display_6_out_7, display_6_out_8,
       display_6_out_9, display_7_out_2, display_7_out_3, display_7_out_4, display_7_out_5, display_7_out_6,
       display_7_out_7, display_7_out_8, display_7_out_9, display_8_out_2, display_8_out_3, display_8_out_4,
       display_8_out_5, display_8_out_6, display_8_out_7, display_8_out_8, display_8_out_9, display_9_out_2,
       display_9_out_3, display_9_out_4, display_9_out_5, display_9_out_6, display_9_out_7, display_9_out_8,
       display_9_out_9, display_10_out_2, display_10_out_3, display_10_out_4, display_10_out_5,
       display_10_out_6, display_10_out_7, display_10_out_8, display_10_out_9, display_11_out_2,
       display_11_out_3, display_11_out_4, display_11_out_5, display_11_out_6, display_11_out_7,
       display_11_out_8, display_11_out_9, display_12_out_2, display_12_out_3, display_12_out_4,
       display_12_out_5, display_12_out_6, display_12_out_7, display_12_out_8, display_12_out_9,
       display_13_out_2, display_13_out_3, display_13_out_4, display_13_out_5, display_13_out_6,
       display_13_out_7, display_13_out_8, display_13_out_9, display_14_out_2, display_14_out_3,
       display_14_out_4, display_14_out_5, display_14_out_6, display_14_out_7, display_14_out_8,
       display_14_out_9, display_15_out_2, display_15_out_3, display_15_out_4, display_15_out_5,
       display_15_out_6, display_15_out_7, display_15_out_8, display_15_out_9, display_16_out_2,
       display_16_out_3, display_16_out_4, display_16_out_5, display_16_out_6, display_16_out_7,
       display_16_out_8, display_16_out_9;
  wire [15:0] n7segment_1_output, n7segment_2_output, ram_1_data, sub_1_out_5, transData;

  LED led_1 (.in(LoadPic));
  Button button_1 (.out(HoldToNextLocation));
  Button button_2 (.out(LoadAlldata));
  Button button_3 (.out(save));
  Button button_4 (.out(resetGame));
  LED led_2 (.in(Load));
  LED led_3 (.in(updatePlayer));
  LED led_4 (.in(LoadTemp));
  autoload autoload_1 (
    .\input (LoadAlldata), .clock(clock), .output_1(LoadPic), .output_2(Load), .output_3(LoadTemp),
    .output_4(updatePlayer));
  Clock clock_1 (.out(clock_1_out));
  and and_1 (and_1_out, clock_2_out, d_ff_1_q);
  Clock clock_2 (.out(clock_2_out));
  not not_1 (not_1_out, d_ff_1_q);
  Register #(.width(4)) register_1 (.D(out_6), .Q(register_1_q), .clk(and_1_out), .clr(resetGame));  // open: en
  LED led_5 (.in(boom));
  LED led_6 (.in(WinTheGame));
  and and_2 (and_2_out, clock_1_out, not_1_out);
  LED led_7 (.in(miss));
  _7segment u_7segment_1 (.\input (out_6), .enable(in_4), .\output (n7segment_1_output));
  D_Flip_Flop d_ff_1 (
    .clk(and_2_out), .D(autoload_2_output_4), .Q(d_ff_1_q), .reset(resetGame));  // open: Qn, preset, en
  DotMatrix #(.matrixcols(8), .matrixrows(8)) dotmatrix_1 (
    .col0(display_1_out_2), .col1(display_1_out_3), .col2(display_1_out_4), .col3(display_1_out_5),
    .col4(display_1_out_6), .col5(display_1_out_7), .col6(display_1_out_8), .col7(display_1_out_9));
  display display_1 (
    .\input (out_8), .out_2(display_1_out_2), .out_3(display_1_out_3), .out_4(display_1_out_4),
    .out_5(display_1_out_5), .out_6(display_1_out_6), .out_7(display_1_out_7), .out_8(display_1_out_8),
    .out_9(display_1_out_9));
  DotMatrix #(.matrixcols(8), .matrixrows(8)) dotmatrix_2 (
    .col0(display_2_out_2), .col1(display_2_out_3), .col2(display_2_out_4), .col3(display_2_out_5),
    .col4(display_2_out_6), .col5(display_2_out_7), .col6(display_2_out_8), .col7(display_2_out_9));
  display display_2 (
    .\input (p4), .out_2(display_2_out_2), .out_3(display_2_out_3), .out_4(display_2_out_4),
    .out_5(display_2_out_5), .out_6(display_2_out_6), .out_7(display_2_out_7), .out_8(display_2_out_8),
    .out_9(display_2_out_9));
  display display_3 (
    .\input (p8), .out_2(display_3_out_2), .out_3(display_3_out_3), .out_4(display_3_out_4),
    .out_5(display_3_out_5), .out_6(display_3_out_6), .out_7(display_3_out_7), .out_8(display_3_out_8),
    .out_9(display_3_out_9));
  DotMatrix #(.matrixcols(8), .matrixrows(8)) dotmatrix_3 (
    .col0(display_3_out_2), .col1(display_3_out_3), .col2(display_3_out_4), .col3(display_3_out_5),
    .col4(display_3_out_6), .col5(display_3_out_7), .col6(display_3_out_8), .col7(display_3_out_9));
  display display_4 (
    .\input (p12), .out_2(display_4_out_2), .out_3(display_4_out_3), .out_4(display_4_out_4),
    .out_5(display_4_out_5), .out_6(display_4_out_6), .out_7(display_4_out_7), .out_8(display_4_out_8),
    .out_9(display_4_out_9));
  DotMatrix #(.matrixcols(8), .matrixrows(8)) dotmatrix_4 (
    .col0(display_4_out_2), .col1(display_4_out_3), .col2(display_4_out_4), .col3(display_4_out_5),
    .col4(display_4_out_6), .col5(display_4_out_7), .col6(display_4_out_8), .col7(display_4_out_9));
  compare compare_1 (
    .action(in_3), .\input (\output ), .position(register_1_q), .Miss_dude(miss), .wow_wowowwowowowow(boom));
  _7_Segment_Display u_7_segment_display_1 (
    .g(n7segment_1_output[8]), .f(n7segment_1_output[9]), .a(n7segment_1_output[10]),
    .b(n7segment_1_output[11]), .e(n7segment_1_output[15]), .d(n7segment_1_output[14]),
    .c(n7segment_1_output[13]), .dp(n7segment_1_output[12]));
  DotMatrix #(.matrixcols(8), .matrixrows(8)) dotmatrix_5 (
    .col0(display_5_out_2), .col1(display_5_out_3), .col2(display_5_out_4), .col3(display_5_out_5),
    .col4(display_5_out_6), .col5(display_5_out_7), .col6(display_5_out_8), .col7(display_5_out_9));
  display display_5 (
    .\input (p1), .out_2(display_5_out_2), .out_3(display_5_out_3), .out_4(display_5_out_4),
    .out_5(display_5_out_5), .out_6(display_5_out_6), .out_7(display_5_out_7), .out_8(display_5_out_8),
    .out_9(display_5_out_9));
  display display_6 (
    .\input (p5), .out_2(display_6_out_2), .out_3(display_6_out_3), .out_4(display_6_out_4),
    .out_5(display_6_out_5), .out_6(display_6_out_6), .out_7(display_6_out_7), .out_8(display_6_out_8),
    .out_9(display_6_out_9));
  DotMatrix #(.matrixcols(8), .matrixrows(8)) dotmatrix_6 (
    .col0(display_6_out_2), .col1(display_6_out_3), .col2(display_6_out_4), .col3(display_6_out_5),
    .col4(display_6_out_6), .col5(display_6_out_7), .col6(display_6_out_8), .col7(display_6_out_9));
  display display_7 (
    .\input (p9), .out_2(display_7_out_2), .out_3(display_7_out_3), .out_4(display_7_out_4),
    .out_5(display_7_out_5), .out_6(display_7_out_6), .out_7(display_7_out_7), .out_8(display_7_out_8),
    .out_9(display_7_out_9));
  DotMatrix #(.matrixcols(8), .matrixrows(8)) dotmatrix_7 (
    .col0(display_7_out_2), .col1(display_7_out_3), .col2(display_7_out_4), .col3(display_7_out_5),
    .col4(display_7_out_6), .col5(display_7_out_7), .col6(display_7_out_8), .col7(display_7_out_9));
  display display_8 (
    .\input (p13), .out_2(display_8_out_2), .out_3(display_8_out_3), .out_4(display_8_out_4),
    .out_5(display_8_out_5), .out_6(display_8_out_6), .out_7(display_8_out_7), .out_8(display_8_out_8),
    .out_9(display_8_out_9));
  DotMatrix #(.matrixcols(8), .matrixrows(8)) dotmatrix_8 (
    .col0(display_8_out_2), .col1(display_8_out_3), .col2(display_8_out_4), .col3(display_8_out_5),
    .col4(display_8_out_6), .col5(display_8_out_7), .col6(display_8_out_8), .col7(display_8_out_9));
  Clock clock_3 (.out(clock));
  _7_Segment_Display u_7_segment_display_2 (
    .g(n7segment_1_output[0]), .f(n7segment_1_output[1]), .a(n7segment_1_output[2]),
    .b(n7segment_1_output[3]), .e(n7segment_1_output[7]), .d(n7segment_1_output[6]),
    .c(n7segment_1_output[5]), .dp(n7segment_1_output[4]));
  display display_9 (
    .\input (p2), .out_2(display_9_out_2), .out_3(display_9_out_3), .out_4(display_9_out_4),
    .out_5(display_9_out_5), .out_6(display_9_out_6), .out_7(display_9_out_7), .out_8(display_9_out_8),
    .out_9(display_9_out_9));
  DotMatrix #(.matrixcols(8), .matrixrows(8)) dotmatrix_9 (
    .col0(display_9_out_2), .col1(display_9_out_3), .col2(display_9_out_4), .col3(display_9_out_5),
    .col4(display_9_out_6), .col5(display_9_out_7), .col6(display_9_out_8), .col7(display_9_out_9));
  DotMatrix #(.matrixcols(8), .matrixrows(8)) dotmatrix_10 (
    .col0(display_10_out_2), .col1(display_10_out_3), .col2(display_10_out_4), .col3(display_10_out_5),
    .col4(display_10_out_6), .col5(display_10_out_7), .col6(display_10_out_8), .col7(display_10_out_9));
  display display_10 (
    .\input (p6), .out_2(display_10_out_2), .out_3(display_10_out_3), .out_4(display_10_out_4),
    .out_5(display_10_out_5), .out_6(display_10_out_6), .out_7(display_10_out_7), .out_8(display_10_out_8),
    .out_9(display_10_out_9));
  DotMatrix #(.matrixcols(8), .matrixrows(8)) dotmatrix_11 (
    .col0(display_11_out_2), .col1(display_11_out_3), .col2(display_11_out_4), .col3(display_11_out_5),
    .col4(display_11_out_6), .col5(display_11_out_7), .col6(display_11_out_8), .col7(display_11_out_9));
  display display_11 (
    .\input (p10), .out_2(display_11_out_2), .out_3(display_11_out_3), .out_4(display_11_out_4),
    .out_5(display_11_out_5), .out_6(display_11_out_6), .out_7(display_11_out_7), .out_8(display_11_out_8),
    .out_9(display_11_out_9));
  display display_12 (
    .\input (p14), .out_2(display_12_out_2), .out_3(display_12_out_3), .out_4(display_12_out_4),
    .out_5(display_12_out_5), .out_6(display_12_out_6), .out_7(display_12_out_7), .out_8(display_12_out_8),
    .out_9(display_12_out_9));
  DotMatrix #(.matrixcols(8), .matrixrows(8)) dotmatrix_12 (
    .col0(display_12_out_2), .col1(display_12_out_3), .col2(display_12_out_4), .col3(display_12_out_5),
    .col4(display_12_out_6), .col5(display_12_out_7), .col6(display_12_out_8), .col7(display_12_out_9));
  and and_3 (\cross , boom, 1'b1);
  display display_13 (
    .\input (p3), .out_2(display_13_out_2), .out_3(display_13_out_3), .out_4(display_13_out_4),
    .out_5(display_13_out_5), .out_6(display_13_out_6), .out_7(display_13_out_7), .out_8(display_13_out_8),
    .out_9(display_13_out_9));
  DotMatrix #(.matrixcols(8), .matrixrows(8)) dotmatrix_13 (
    .col0(display_13_out_2), .col1(display_13_out_3), .col2(display_13_out_4), .col3(display_13_out_5),
    .col4(display_13_out_6), .col5(display_13_out_7), .col6(display_13_out_8), .col7(display_13_out_9));
  display display_14 (
    .\input (p7), .out_2(display_14_out_2), .out_3(display_14_out_3), .out_4(display_14_out_4),
    .out_5(display_14_out_5), .out_6(display_14_out_6), .out_7(display_14_out_7), .out_8(display_14_out_8),
    .out_9(display_14_out_9));
  DotMatrix #(.matrixcols(8), .matrixrows(8)) dotmatrix_14 (
    .col0(display_14_out_2), .col1(display_14_out_3), .col2(display_14_out_4), .col3(display_14_out_5),
    .col4(display_14_out_6), .col5(display_14_out_7), .col6(display_14_out_8), .col7(display_14_out_9));
  DotMatrix #(.matrixcols(8), .matrixrows(8)) dotmatrix_15 (
    .col0(display_15_out_2), .col1(display_15_out_3), .col2(display_15_out_4), .col3(display_15_out_5),
    .col4(display_15_out_6), .col5(display_15_out_7), .col6(display_15_out_8), .col7(display_15_out_9));
  display display_15 (
    .\input (p11), .out_2(display_15_out_2), .out_3(display_15_out_3), .out_4(display_15_out_4),
    .out_5(display_15_out_5), .out_6(display_15_out_6), .out_7(display_15_out_7), .out_8(display_15_out_8),
    .out_9(display_15_out_9));
  display display_16 (
    .\input (p15), .out_2(display_16_out_2), .out_3(display_16_out_3), .out_4(display_16_out_4),
    .out_5(display_16_out_5), .out_6(display_16_out_6), .out_7(display_16_out_7), .out_8(display_16_out_8),
    .out_9(display_16_out_9));
  DotMatrix #(.matrixcols(8), .matrixrows(8)) dotmatrix_16 (
    .col0(display_16_out_2), .col1(display_16_out_3), .col2(display_16_out_4), .col3(display_16_out_5),
    .col4(display_16_out_6), .col5(display_16_out_7), .col6(display_16_out_8), .col7(display_16_out_9));
  and and_4 (unknown, miss, 1'b1);
  assign bit_extender_1_out = {{2{1'b0}}, out_9};  // Bit_Extender bit_extender_1
  sub sub_1 (.\input (\output ), .position(out_6), .clock(boom), .out_5(sub_1_out_5));  // open: clear
  _7segment u_7segment_2 (.\input (bit_extender_1_out), .enable(in_5), .\output (n7segment_2_output));
  Multiplexer #(.width(16)) multiplexer_1 (
    .in0(transData), .in1(sub_1_out_5), .out(out_11), .sel(d_ff_2_q));  // open: en
  _7_Segment_Display u_7_segment_display_3 (
    .g(n7segment_2_output[8]), .f(n7segment_2_output[9]), .a(n7segment_2_output[10]),
    .b(n7segment_2_output[11]), .e(n7segment_2_output[15]), .d(n7segment_2_output[14]),
    .c(n7segment_2_output[13]), .dp(n7segment_2_output[12]));
  Button button_5 (.out(button_5_out));
  D_Flip_Flop d_ff_2 (
    .clk(clock), .D(autoload_2_output_4), .Q(d_ff_2_q), .Qn(d_ff_2_qn), .en(d_ff_2_qn), .reset(resetGame));  // open: preset
  _7_Segment_Display u_7_segment_display_4 (
    .g(n7segment_2_output[0]), .f(n7segment_2_output[1]), .a(n7segment_2_output[2]),
    .b(n7segment_2_output[3]), .e(n7segment_2_output[7]), .d(n7segment_2_output[6]),
    .c(n7segment_2_output[5]), .dp(n7segment_2_output[4]));
  autoload autoload_2 (
    .\input (button_5_out), .clock(clock), .output_1(autoload_2_output_1), .output_2(autoload_2_output_2),
    .output_3(autoload_2_output_3), .output_4(autoload_2_output_4));
  holdTobutton holdtobutton_1 (.\input (boom), .in_2(clock), .\output (holdtobutton_1_output));
  Cursor cursor_1 (
    .picSelect(picselector_1_output), .next(HoldToNextLocation), .\output (out_10), .position(out_6),
    .in_4(clock), .load(LoadPic), .clear(resetGame));  // open: count
  adder adder_1 (
    .in_1(holdtobutton_1_output), .clock(clock), .clear(resetGame), .\output (adder_1_output), .score(out_9));
  RAM #(.addrWidth(2), .dataWidth(16), .bus("separate")) ram_1 (
    .addr(2'b00), .din(out_11), .data(ram_1_data), .clk(autoload_2_output_1), .ld(autoload_2_output_2),
    .clr(resetGame));  // open: str, sel
  Demultiplexer #(.select(4)) demultiplexer_1 (
    .out0(UpdateTemp0), .out1(UpdateTemp1), .out2(UpdateTemp2), .out3(UpdateTemp3), .out4(UpdateTemp4),
    .out5(UpdateTemp5), .out6(UpdateTemp6), .out7(UpdateTemp7), .out8(UpdateTemp8), .out9(UpdateTemp9),
    .out10(UpdateTemp10), .out11(UpdateTemp11), .out12(UpdateTemp12), .out13(UpdateTemp13),
    .out14(UpdateTemp14), .out15(UpdateTemp15), .in(clock), .sel(out_6));  // open: en
  Register #(.width(16)) register_2 (
    .D(ram_1_data), .Q(\output ), .clk(autoload_2_output_3), .clr(resetGame));  // open: en
  and and_5 (WinTheGame, 1'b1, adder_1_output);
  picSelector picselector_1 (.unknown(unknown), .\cross (\cross ), .ship(in_1), .\output (picselector_1_output));
  holdTobutton holdtobutton_2 (.\input (d_ff_3_q), .in_2(clock), .\output (clear));
  D_Flip_Flop d_ff_3 (
    .clk(clock), .D(autoload_2_output_4), .Q(d_ff_3_q), .en(not_2_out), .reset(resetGame));  // open: Qn, preset
  not not_2 (not_2_out, d_ff_3_q);
  Demultiplexer #(.select(4), .width(3)) demultiplexer_2 (
    .out0(demultiplexer_2_out0), .out1(demultiplexer_2_out1), .out2(demultiplexer_2_out2),
    .out3(demultiplexer_2_out3), .out4(demultiplexer_2_out4), .out5(demultiplexer_2_out5),
    .out6(demultiplexer_2_out6), .out7(demultiplexer_2_out7), .out8(demultiplexer_2_out8),
    .out9(demultiplexer_2_out9), .out10(demultiplexer_2_out10), .out11(demultiplexer_2_out11),
    .out12(demultiplexer_2_out12), .out13(demultiplexer_2_out13), .out14(demultiplexer_2_out14),
    .out15(demultiplexer_2_out15), .in(out_10), .sel(out_6));  // open: en
  tempDisplay tempdisplay_1 (
    .data(demultiplexer_2_out0), .clear(clear), .\input (LoadTemp), .cock(UpdateTemp0), .\output (out_8));
  tempDisplay tempdisplay_2 (
    .data(demultiplexer_2_out1), .clear(clear), .\input (LoadTemp), .cock(UpdateTemp1), .\output (p1));
  tempDisplay tempdisplay_3 (
    .data(demultiplexer_2_out2), .clear(clear), .\input (LoadTemp), .cock(UpdateTemp2), .\output (p2));
  tempDisplay tempdisplay_4 (
    .data(demultiplexer_2_out3), .clear(clear), .\input (LoadTemp), .cock(UpdateTemp3), .\output (p3));
  tempDisplay tempdisplay_5 (
    .data(demultiplexer_2_out4), .clear(clear), .\input (LoadTemp), .cock(UpdateTemp4), .\output (p4));
  tempDisplay tempdisplay_6 (
    .data(demultiplexer_2_out5), .clear(clear), .\input (LoadTemp), .cock(UpdateTemp5), .\output (p5));
  tempDisplay tempdisplay_7 (
    .data(demultiplexer_2_out6), .clear(clear), .\input (LoadTemp), .cock(UpdateTemp6), .\output (p6));
  tempDisplay tempdisplay_8 (
    .data(demultiplexer_2_out7), .clear(clear), .\input (LoadTemp), .cock(UpdateTemp7), .\output (p7));
  tempDisplay tempdisplay_9 (
    .data(demultiplexer_2_out8), .clear(clear), .\input (LoadTemp), .cock(UpdateTemp8), .\output (p8));
  tempDisplay tempdisplay_10 (
    .data(demultiplexer_2_out9), .clear(clear), .\input (LoadTemp), .cock(UpdateTemp9), .\output (p9));
  tempDisplay tempdisplay_11 (
    .data(demultiplexer_2_out10), .clear(clear), .\input (LoadTemp), .cock(UpdateTemp10), .\output (p10));
  tempDisplay tempdisplay_12 (
    .data(demultiplexer_2_out11), .clear(clear), .\input (LoadTemp), .cock(UpdateTemp11), .\output (p11));
  tempDisplay tempdisplay_13 (
    .data(demultiplexer_2_out12), .clear(clear), .\input (LoadTemp), .cock(UpdateTemp12), .\output (p12));
  check check_1 (.\input (out_8), .\output (transData[0]));
  check check_2 (.\input (p1), .\output (transData[1]));
  check check_3 (.\input (p2), .\output (transData[2]));
  check check_4 (.\input (p3), .\output (transData[3]));
  check check_5 (.\input (p4), .\output (transData[4]));
  check check_6 (.\input (p5), .\output (transData[5]));
  check check_7 (.\input (p6), .\output (transData[6]));
  check check_8 (.\input (p7), .\output (transData[7]));
  check check_9 (.\input (p8), .\output (transData[8]));
  check check_10 (.\input (p9), .\output (transData[9]));
  check check_11 (.\input (p10), .\output (transData[10]));
  check check_12 (.\input (p11), .\output (transData[11]));
  check check_13 (.\input (p12), .\output (transData[12]));
  check check_14 (.\input (p13), .\output (transData[13]));
  check check_15 (.\input (p14), .\output (transData[14]));
  check check_16 (.\input (p15), .\output (transData[15]));
  tempDisplay tempdisplay_14 (
    .data(demultiplexer_2_out13), .clear(clear), .\input (LoadTemp), .cock(UpdateTemp13), .\output (p13));
  tempDisplay tempdisplay_15 (
    .data(demultiplexer_2_out14), .clear(clear), .\input (LoadTemp), .cock(UpdateTemp14), .\output (p14));
  tempDisplay tempdisplay_16 (
    .data(demultiplexer_2_out15), .clear(clear), .\input (LoadTemp), .cock(UpdateTemp15), .\output (p15));

  assign output_2 = \output ;

  // Other names for the same wires on the sheet: _7segmentEnable = in_4; clearScore = in_2; fire = in_3;
  //   outputcheck[15:0] = \output ; p0[2:0] = out_8; picData[2:0] = out_10; position[3:0] = out_6; score[1:0] = out_9;
  //   ship = in_1; updatePosition = clock
endmodule

module display (
  input  [2:0] \input ,
  output [7:0] out_2,
  output [7:0] out_3,
  output [7:0] out_4,
  output [7:0] out_5,
  output [7:0] out_6,
  output [7:0] out_7,
  output [7:0] out_8,
  output [7:0] out_9
);

  ROM #(.addrWidth(3)) rom_1 (.addr(\input ), .data(out_2));  // open: sel
  ROM #(.addrWidth(3)) rom_2 (.addr(\input ), .data(out_3));  // open: sel
  ROM #(.addrWidth(3)) rom_3 (.addr(\input ), .data(out_4));  // open: sel
  ROM #(.addrWidth(3)) rom_4 (.addr(\input ), .data(out_5));  // open: sel
  ROM #(.addrWidth(3)) rom_5 (.addr(\input ), .data(out_6));  // open: sel
  ROM #(.addrWidth(3)) rom_6 (.addr(\input ), .data(out_7));  // open: sel
  ROM #(.addrWidth(3)) rom_7 (.addr(\input ), .data(out_8));  // open: sel
  ROM #(.addrWidth(3)) rom_8 (.addr(\input ), .data(out_9));  // open: sel
  DotMatrix #(.matrixcols(8), .matrixrows(8)) dotmatrix_1 (
    .col0(out_2), .col1(out_3), .col2(out_4), .col3(out_5), .col4(out_6), .col5(out_7), .col6(out_8),
    .col7(out_9));

  // Notes on the sheet:
  //   contents of rom_1 (hex, n*v repeats v):
  //   0 ff 0 ff 0 ff 0 ff
  //   contents of rom_2 (hex, n*v repeats v):
  //   0 81 4 85 42 c3 0 81
  //   contents of rom_3 (hex, n*v repeats v):
  //   0 81 6 87 24 a5 30 b1
  //   contents of rom_4 (hex, n*v repeats v):
  //   0 81 7e ff 18 99 40 c1
  //   contents of rom_5 (hex, n*v repeats v):
  //   0 81 66 e7 18 99 5a db
  //   contents of rom_6 (hex, n*v repeats v):
  //   0 81 26 a7 24 a5 30 b1
  //   contents of rom_7 (hex, n*v repeats v):
  //   0 81 4 85 42 c3 0 81
  //   contents of rom_8 (hex, n*v repeats v):
  //   0 ff 0 ff 0 ff 0 ff
endmodule

module Cursor (
  input  [2:0] picSelect,
  input  next,
  input  load,
  input  in_4,
  input  clear,
  output count,
  output [2:0] \output ,
  output [3:0] position
);

  wire autoload_1_output_2;
  wire [3:0] adder_1_out, bit_extender_1_out;

  and and_1 (count, next, in_4);
  Adder #(.width(4)) adder_1 (.a(position), .b(bit_extender_1_out), .out(adder_1_out));  // open: cin, cout
  assign bit_extender_1_out = {{3{1'b0}}, next};  // Bit_Extender bit_extender_1
  Register #(.width(4)) register_1 (.D(adder_1_out), .Q(position), .clk(in_4));  // open: en, clr
  RAM #(.addrWidth(4), .dataWidth(3), .bus("separate")) ram_1 (
    .addr(position), .din(picSelect), .data(\output ), .clk(in_4), .ld(load), .clr(autoload_1_output_2));  // open: str, sel
  autoload autoload_1 (
    .\input (clear), .clock(in_4), .output_1(load), .output_2(autoload_1_output_2));  // open: output_3, output_4

  // Notes on the sheet:
  //   เลื่อน cursor ต้องกด next แล้วตามด้วย clock
endmodule

module tempDisplay (
  input  [2:0] data,
  input  clear,
  input  \input ,
  input  cock,
  output [2:0] \output 
);

  wire autoload_1_output_1, autoload_1_output_2, autoload_1_output_3;
  wire [2:0] ram_1_data;

  RAM #(.addrWidth(2), .dataWidth(3), .bus("separate")) ram_1 (
    .addr(2'b00), .din(data), .data(ram_1_data), .clk(autoload_1_output_1), .ld(autoload_1_output_2),
    .clr(clear));  // open: str, sel
  autoload autoload_1 (
    .\input (\input ), .clock(cock), .output_1(autoload_1_output_1), .output_2(autoload_1_output_2),
    .output_3(autoload_1_output_3));  // open: output_4
  Register #(.width(3)) register_1 (.D(ram_1_data), .Q(\output ), .clk(autoload_1_output_3), .clr(clear));  // open: en
endmodule

module picSelector (
  input  unknown,
  input  \cross ,
  input  ship,
  output [2:0] \output 
);

  Multiplexer #(.select(3), .width(3)) multiplexer_1 (
    .in0(3'b000), .in1(3'b010), .in2(3'b100), .in3(3'b000), .in4(3'b110), .in5(3'b000), .in6(3'b000),
    .in7(3'b000), .out(\output ), .sel({unknown, \cross , ship}));  // open: en

  // Other names for the same wires on the sheet: shup = ship
endmodule

module autoload (
  input  \input ,
  input  clock,
  output output_1,
  output output_2,
  output output_3,
  output output_4
);

  wire and_1_out, d_ff_1_q, d_ff_5_q, d_ff_6_q, multiplexer_1_out, not_1_out;

  not not_1 (not_1_out, 1'b1);
  Multiplexer multiplexer_1 (.in0(not_1_out), .in1(1'b1), .out(multiplexer_1_out), .sel(\input ));  // open: en
  D_Flip_Flop d_ff_1 (
    .clk(clock), .D(multiplexer_1_out), .Q(d_ff_1_q), .preset(and_1_out), .reset(d_ff_6_q));  // open: Qn, en
  and and_1 (and_1_out, output_1, d_ff_1_q);
  Multiplexer multiplexer_2 (.in0(1'b0), .in1(1'b1), .out(output_1), .sel(d_ff_1_q));  // open: en
  D_Flip_Flop d_ff_2 (.clk(clock), .D(output_1), .Q(output_2));  // open: Qn, preset, en, reset
  D_Flip_Flop d_ff_3 (.clk(clock), .D(output_2), .Q(output_3));  // open: Qn, preset, en, reset
  D_Flip_Flop d_ff_4 (.clk(clock), .D(output_3), .Q(output_4));  // open: Qn, preset, en, reset
  D_Flip_Flop d_ff_5 (.clk(clock), .D(output_4), .Q(d_ff_5_q));  // open: Qn, preset, en, reset
  D_Flip_Flop d_ff_6 (.clk(clock), .D(d_ff_5_q), .Q(d_ff_6_q));  // open: Qn, preset, en, reset
endmodule

module _7segment (
  input  [3:0] \input ,
  input  enable,
  output [15:0] \output 
);

  wire [3:0] multiplexer_1_out;

  Multiplexer #(.width(4)) multiplexer_1 (
    .in0(\input ), .in1(4'b0000), .out(multiplexer_1_out), .sel(enable));  // open: en
  ROM #(.addrWidth(4), .dataWidth(16)) rom_1 (.addr(multiplexer_1_out), .data(\output ));  // open: sel
  _7_Segment_Display u_7_segment_display_1 (
    .g(\output [8]), .f(\output [9]), .a(\output [10]), .b(\output [11]), .e(\output [15]), .d(\output [14]),
    .c(\output [13]), .dp(\output [12]));
  _7_Segment_Display u_7_segment_display_2 (
    .g(\output [0]), .f(\output [1]), .a(\output [2]), .b(\output [3]), .e(\output [7]), .d(\output [6]),
    .c(\output [5]), .dp(\output [4]));

  // Notes on the sheet:
  //   contents of rom_1 (hex, n*v repeats v):
  //   eeee ee28 eecd ee6d ee2b ee67 eee7 ee2e eeef ee6f 28ee 2828 28cd 286d 282b 2867
endmodule

module check (
  input  [2:0] \input ,
  output \output 
);

  Multiplexer #(.select(3)) multiplexer_1 (
    .in0(1'b0), .in1(1'b0), .in2(1'b1), .in3(1'b0), .in4(1'b0), .in5(1'b0), .in6(1'b0), .in7(1'b0),
    .out(\output ), .sel(\input ));  // open: en
endmodule

module compare (
  input  action,
  input  [15:0] \input ,
  input  [3:0] position,
  output Miss_dude,
  output wow_wowowwowowowow
);

  wire multiplexer_1_out, not_1_out;

  Multiplexer #(.select(4)) multiplexer_1 (
    .in0(\input [0]), .in1(\input [1]), .in2(\input [2]), .in3(\input [3]), .in4(\input [4]),
    .in5(\input [5]), .in6(\input [6]), .in7(\input [7]), .in8(\input [8]), .in9(\input [9]),
    .in10(\input [10]), .in11(\input [11]), .in12(\input [12]), .in13(\input [13]), .in14(\input [14]),
    .in15(\input [15]), .out(multiplexer_1_out), .sel(position));  // open: en
  and and_1 (wow_wowowwowowowow, action, multiplexer_1_out);
  not not_1 (not_1_out, wow_wowowwowowowow);
  and and_2 (Miss_dude, action, not_1_out);
endmodule

module savePlayerData (
  input  [2:0] input0,
  input  [2:0] input1,
  input  [2:0] input2,
  input  [2:0] input3,
  input  [2:0] input4,
  input  [2:0] input5,
  input  [2:0] input6,
  input  [2:0] input7,
  input  [2:0] input8,
  input  \input ,
  input  clear,
  input  [2:0] input9,
  input  clock,
  input  [2:0] input10,
  input  [2:0] input11,
  input  [2:0] input12,
  input  [2:0] input13,
  input  [2:0] input14,
  input  [2:0] input15,
  output [15:0] out_20,
  output [15:0] \output 
);

  wire autoload_1_output_1, autoload_1_output_2, autoload_1_output_3;
  wire [15:0] ram_1_data;

  check check_1 (.\input (input0), .\output (out_20[0]));
  check check_2 (.\input (input1), .\output (out_20[1]));
  check check_3 (.\input (input2), .\output (out_20[2]));
  check check_4 (.\input (input3), .\output (out_20[3]));
  check check_5 (.\input (input4), .\output (out_20[4]));
  check check_6 (.\input (input5), .\output (out_20[5]));
  check check_7 (.\input (input6), .\output (out_20[6]));
  check check_8 (.\input (input7), .\output (out_20[7]));
  check check_9 (.\input (input8), .\output (out_20[8]));
  check check_10 (.\input (input9), .\output (out_20[9]));
  check check_11 (.\input (input10), .\output (out_20[10]));
  check check_12 (.\input (input11), .\output (out_20[11]));
  check check_13 (.\input (input12), .\output (out_20[12]));
  check check_14 (.\input (input13), .\output (out_20[13]));
  check check_15 (.\input (input14), .\output (out_20[14]));
  check check_16 (.\input (input15), .\output (out_20[15]));
  autoload autoload_1 (
    .\input (\input ), .clock(clock), .output_1(autoload_1_output_1), .output_2(autoload_1_output_2),
    .output_3(autoload_1_output_3));  // open: output_4
  RAM #(.addrWidth(2), .dataWidth(16), .bus("separate")) ram_1 (
    .addr(2'b00), .din(out_20), .data(ram_1_data), .clk(autoload_1_output_1), .ld(autoload_1_output_2),
    .clr(clear));  // open: str, sel
  Register #(.width(16)) register_1 (.D(ram_1_data), .Q(\output ), .clk(autoload_1_output_3));  // open: en, clr
endmodule

module buttontoswitch (
  input  instantReeset,
  input  \input ,
  input  clock,
  output \output 
);

  wire and_1_out, and_2_out, and_3_out, and_5_out, autoload_1_output_4, multiplexer_1_out, not_1_out,
       not_2_out, not_3_out, not_4_out, not_5_out, or_1_out, register_1_q;

  and and_1 (and_1_out, not_2_out, autoload_1_output_4, not_1_out);
  not not_1 (not_1_out, \input );
  not not_2 (not_2_out, \output );
  not not_3 (not_3_out, register_1_q);
  or or_1 (or_1_out, and_1_out, and_2_out);
  and and_2 (and_2_out, \input , \input , not_3_out);
  Register #(.width(1)) register_1 (.D(or_1_out), .Q(register_1_q), .clk(and_3_out));  // open: en, clr
  and and_3 (and_3_out, clock, not_4_out);
  not not_4 (not_4_out, register_1_q);
  not not_5 (not_5_out, multiplexer_1_out);
  Multiplexer multiplexer_1 (
    .in0(autoload_1_output_4), .in1(1'b0), .out(multiplexer_1_out), .sel(instantReeset));  // open: en
  and and_4 (\output , register_1_q, not_5_out);
  and and_5 (and_5_out, \output , clock);
  autoload autoload_1 (
    .\input (register_1_q), .clock(and_5_out), .output_4(autoload_1_output_4));  // open: output_1, output_2, output_3
endmodule

module adder (
  input  in_1,
  input  clock,
  input  clear,
  output \output ,
  output [1:0] score
);

  wire and_1_out, d_ff_1_q, not_1_out, not_2_out;
  wire [1:0] adder_1_out, bit_extender_1_out;

  assign bit_extender_1_out = {{1{1'b0}}, in_1};  // Bit_Extender bit_extender_1
  not not_1 (not_1_out, d_ff_1_q);
  Adder #(.width(2)) adder_1 (.a(score), .b(bit_extender_1_out), .out(adder_1_out));  // open: cin, cout
  Register #(.width(2)) register_1 (.D(adder_1_out), .en(not_1_out), .Q(score), .clk(clock), .clr(clear));
  Multiplexer #(.select(2)) multiplexer_1 (
    .in0(1'b0), .in1(1'b0), .in2(1'b0), .in3(1'b1), .out(\output ), .sel(score));  // open: en
  not not_2 (not_2_out, d_ff_1_q);
  and and_1 (and_1_out, clock, not_2_out);
  D_Flip_Flop d_ff_1 (.clk(and_1_out), .D(\output ), .Q(d_ff_1_q));  // open: Qn, preset, en, reset
endmodule

module sub (
  input  [15:0] \input ,
  input  clock,
  input  clear,
  input  [3:0] position,
  output [15:0] out_5
);

  wire [15:0] multiplexer_1_out, subtractor_1_out;

  Multiplexer #(.select(4), .width(16)) multiplexer_1 (
    .in0(16'h1), .in1(16'h2), .in2(16'h4), .in3(16'h8), .in4(16'h10), .in5(16'h20), .in6(16'h40),
    .in7(16'h80), .in8(16'h100), .in9(16'h200), .in10(16'h400), .in11(16'h800), .in12(16'h1000),
    .in13(16'h2000), .in14(16'h4000), .in15(16'h8000), .out(multiplexer_1_out), .sel(position));  // open: en
  Subtractor #(.width(16)) subtractor_1 (
    .a(\input ), .b(multiplexer_1_out), .out(subtractor_1_out));  // open: bin, bout
  Register #(.width(16)) register_1 (.D(subtractor_1_out), .Q(out_5), .clk(clock), .clr(clear));  // open: en
endmodule

module holdTobutton (
  input  \input ,
  input  in_2,
  output \output 
);

  wire and_1_out, and_2_out, d_ff_1_q, d_ff_3_q, multiplexer_1_out, multiplexer_2_out, not_1_out, not_2_out,
       not_3_out, not_4_out, not_5_out, or_1_out, or_2_out;

  not not_1 (not_1_out, d_ff_1_q);
  not not_2 (not_2_out, multiplexer_2_out);
  not not_3 (not_3_out, \input );
  D_Flip_Flop d_ff_1 (.clk(in_2), .D(and_1_out), .Q(d_ff_1_q), .en(not_1_out), .reset(not_4_out));  // open: Qn, preset
  not not_4 (not_4_out, and_2_out);
  and and_1 (and_1_out, not_2_out, not_3_out);
  and and_2 (and_2_out, and_1_out, and_1_out, d_ff_3_q);
  D_Flip_Flop d_ff_2 (.clk(in_2), .D(\input ), .Q(\output ), .en(or_1_out), .reset(not_5_out));  // open: Qn, preset
  not not_5 (not_5_out, or_1_out);
  or or_1 (or_1_out, d_ff_1_q, multiplexer_1_out);
  Multiplexer multiplexer_1 (.in0(1'b1), .in1(1'b0), .out(multiplexer_1_out), .sel(d_ff_3_q));  // open: en
  D_Flip_Flop d_ff_3 (.clk(in_2), .D(\output ), .Q(d_ff_3_q), .en(or_2_out));  // open: Qn, preset, reset
  or or_2 (or_2_out, or_1_out, multiplexer_2_out);
  Multiplexer multiplexer_2 (.in0(1'b1), .in1(1'b0), .out(multiplexer_2_out), .sel(d_ff_3_q));  // open: en
endmodule
